# Fritzing sketch Configurazione_Circuito (saved by Fritzing 0.9.9b)
breadboards: 1

parts:
  J1 = STM32 Nucleo boards
  S1 = Pushbutton [package="[THT]"]
  S2 = Pushbutton [package="[THT]"]
  S3 = Pushbutton [package="[THT]"]
  S4 = Pushbutton [package="[THT]"]
  LED1 = RGB LED (com. cathode, rbg) [package="5 mm [THT]"]
  LED2 = LED - 5mm [color="Yellow (595nm)" package="5 mm [THT]"]
  LED3 = LED - 5mm [color="Yellow (595nm)" package="5 mm [THT]"]
  WeMos_D1_Mini_Relay_Shield_V1 = WeMos D1 Mini Relay Shield
  R1 = Resistor [tolerance=±5% resistance=220 package="0603 [SMD]"]
  LED4 = LED - 5mm [color="Green (570nm)" package="5 mm [THT]"]
  R2 = Resistor [tolerance=±5% resistance=220 package="0603 [SMD]"]
  R3 = Resistor [tolerance=±5% resistance=220 package="0603 [SMD]"]
  R4 = Resistor [tolerance=±5% resistance=220 package="0603 [SMD]"]
  R5 = Resistor [tolerance=±5% resistance=220 package="0603 [SMD]"]
  J3 = Basic Servo

nets:
  N1: J1.GND#333, LED1.common_cathode, LED2.cathode, LED3.cathode, LED4.cathode, J3.gnd
  N2: J1.3v3, S1.Pin_3, S1.Pin_4, S2.Pin_3, S2.Pin_4, S3.Pin_3, S3.Pin_4, S4.Pin_3, S4.Pin_4, WeMos_D1_Mini_Relay_Shield_V1.COM
  5V: J1.5V, WeMos_D1_Mini_Relay_Shield_V1.5V, J3.vcc
  N3: J1.PC9, R5.Pin_0
  N4: J1.PA5, R1.Pin_0
  N5: J1.PA6, R4.Pin_0
  N6: J1.PB6, J3.pulse
  N7: J1.PC7, R3.Pin_0
  N8: J1.GND#3310, WeMos_D1_Mini_Relay_Shield_V1.G
  N9: J1.PB0, S2.Pin_1, S2.Pin_2
  N10: J1.PC10, S3.Pin_1, S3.Pin_2
  N11: J1.PA15, S4.Pin_1, S4.Pin_2
  N12: J1.PC13, S1.Pin_1, S1.Pin_2
  N13: J1.PC2, WeMos_D1_Mini_Relay_Shield_V1.D1
  N14: LED1.red_anode, R4.Pin_1
  N15: LED1.blue_anode, R5.Pin_1
  N16: LED1.green_anode, R3.Pin_1
  N17: LED2.anode, LED3.anode, R2.Pin_1
  N18: WeMos_D1_Mini_Relay_Shield_V1.NO, R2.Pin_0
  N19: R1.Pin_1, LED4.anode
